// Logisim project watermelon_one.circ as structural Verilog: 5 circuits, main circuit main
module main (
);

  program_counter program_counter_1 ();  // open: Y, D, SWIN, OE, C, CL, O
  // ROM #(.addrWidth(19), .line("quad")) rom_1: pin names not known
endmodule

module octal_D_flip_flop (
  input  OE,
  input  C,
  input  CL,
  input  [7:0] D,
  output [7:0] O
);

  wire [7:0] d_ff_1_q;

  D_Flip_Flop d_ff_1 (.D(D[0]), .clk(C), .Q(d_ff_1_q[0]), .reset(CL));  // open: Qn, preset
  D_Flip_Flop d_ff_2 (.D(D[1]), .clk(C), .Q(d_ff_1_q[1]), .reset(CL));  // open: Qn, preset
  D_Flip_Flop d_ff_3 (.D(D[2]), .clk(C), .Q(d_ff_1_q[2]), .reset(CL));  // open: Qn, preset
  D_Flip_Flop d_ff_4 (.D(D[3]), .clk(C), .Q(d_ff_1_q[3]), .reset(CL));  // open: Qn, preset
  D_Flip_Flop d_ff_5 (.D(D[4]), .clk(C), .Q(d_ff_1_q[4]), .reset(CL));  // open: Qn, preset
  D_Flip_Flop d_ff_6 (.D(D[5]), .clk(C), .Q(d_ff_1_q[5]), .reset(CL));  // open: Qn, preset
  D_Flip_Flop d_ff_7 (.D(D[6]), .clk(C), .Q(d_ff_1_q[6]), .reset(CL));  // open: Qn, preset
  D_Flip_Flop d_ff_8 (.D(D[7]), .clk(C), .Q(d_ff_1_q[7]), .reset(CL));  // open: Qn, preset
  assign O = OE ? d_ff_1_q : 8'bz;  // Controlled_Buffer controlled_buffer_1
endmodule

module register_8_bit (
  input  OE,
  input  WE,
  input  C,
  input  CL,
  input  [7:0] D,
  output [7:0] O
);

  wire and_1_out;

  and and_1 (and_1_out, WE, C);
  octal_D_flip_flop octal_d_flip_flop_1 (.OE(OE), .C(and_1_out), .CL(CL), .D(D), .O(O));
endmodule

module program_counter (
  input  [31:0] Y,
  input  [31:0] D,
  input  SWIN,
  input  OE,
  input  C,
  input  CL,
  output [31:0] O
);

  wire [7:0] multiplexer_1_out, multiplexer_2_out, multiplexer_3_out, multiplexer_4_out;
  wire [31:0] adder_1_out;

  Multiplexer #(.width(8)) multiplexer_1 (.in0(adder_1_out[7:0]), .in1(D[7:0]), .out(multiplexer_1_out), .sel(SWIN));
  Adder #(.width(32)) adder_1 (.a(Y), .b(O), .out(adder_1_out));  // open: cin, cout
  Multiplexer #(.width(8)) multiplexer_2 (.in0(adder_1_out[15:8]), .in1(D[15:8]), .out(multiplexer_2_out), .sel(SWIN));
  Multiplexer #(.width(8)) multiplexer_3 (
    .in0(adder_1_out[23:16]), .in1(D[23:16]), .out(multiplexer_3_out), .sel(SWIN));
  Multiplexer #(.width(8)) multiplexer_4 (
    .in0(adder_1_out[31:24]), .in1(D[31:24]), .out(multiplexer_4_out), .sel(SWIN));
  octal_D_flip_flop octal_d_flip_flop_1 (.OE(OE), .C(C), .CL(CL), .D(multiplexer_1_out), .O(O[7:0]));
  octal_D_flip_flop octal_d_flip_flop_2 (.OE(OE), .C(C), .CL(CL), .D(multiplexer_2_out), .O(O[15:8]));
  octal_D_flip_flop octal_d_flip_flop_3 (.OE(OE), .C(C), .CL(CL), .D(multiplexer_3_out), .O(O[23:16]));
  octal_D_flip_flop octal_d_flip_flop_4 (.OE(OE), .C(C), .CL(CL), .D(multiplexer_4_out), .O(O[31:24]));

  // Notes on the sheet:
  //   Y: initial=0x4
endmodule

module register_file (
  input  [4:0] R1A,
  input  [4:0] R2A,
  input  WRITE,
  input  LOAD,
  input  CLOCK,
  input  [4:0] WRITE_ADDR,
  input  [31:0] WRITE_DATA,
  output [31:0] R1O,
  output [31:0] R2O
);

  RAM #(.addrWidth(5), .databus("bidir"), .enables("line")) ram_1 ();  // open: addr, we, oe, clk, data

  // Other names for the same wires on the sheet: read_reg_1_adr[4:0] = R1A; read_reg_2_adr[4:0] = R2A;
  //   reg_1_out[31:0] = R1O; reg_2_out[31:0] = R2O
endmodule
